// Logisim project counter_bcd.circ as structural Verilog: 1 circuit, main circuit main
module main (
);

  wire CLOCK, clock_1_out, comparator_1_eq, comparator_2_eq, comparator_3_eq, comparator_4_eq,
       comparator_5_eq, j_k_ff_1_q, j_k_ff_2_q;
  wire [7:0] counter_1_q, divider_1_out, divider_1_rem, divider_2_out, divider_2_rem, undriven, undriven_2,
       undriven_3, undriven_4, undriven_5;

  Clock clock_1 (.out(clock_1_out));
  Counter #(.width(8), .max('hf)) counter_1 (
    .clr(1'b0), .clk(clock_1_out), .Q(counter_1_q));  // open: load, up, count, D, carry
  Divider #(.width(8)) divider_1 (.a(undriven), .b(8'h64), .out(divider_1_out), .rem(divider_1_rem));  // open: upper
  Comparator #(.width(8)) comparator_1 (.a(undriven_2), .b(8'h2), .eq(comparator_1_eq));  // open: gt, lt
  Comparator #(.width(8)) comparator_2 (.a(undriven_3), .b(8'h2), .eq(comparator_2_eq));  // open: gt, lt
  Comparator #(.width(8)) comparator_3 (.a(undriven_4), .b(8'ha), .eq(comparator_3_eq));  // open: gt, lt
  Comparator #(.width(8)) comparator_4 (.a(undriven_5), .b(8'h5), .eq(comparator_4_eq));  // open: gt, lt
  Comparator #(.width(8)) comparator_5 (.a(undriven), .b(8'ha), .eq(comparator_5_eq));  // open: gt, lt
  Hex_Digit_Display hex_digit_display_1 (.value(divider_1_out[3:0]));  // open: dp
  LED led_1 (.in(comparator_1_eq));
  Divider #(.width(8)) divider_2 (
    .a(divider_1_rem), .b(8'ha), .out(divider_2_out), .rem(divider_2_rem));  // open: upper
  J_K_Flip_Flop j_k_ff_1 (
    .J(comparator_2_eq), .K(comparator_3_eq), .clk(CLOCK), .Q(j_k_ff_1_q));  // open: Qn, preset, reset
  J_K_Flip_Flop j_k_ff_2 (
    .J(comparator_4_eq), .K(comparator_5_eq), .clk(CLOCK), .Q(j_k_ff_2_q));  // open: Qn, preset, reset
  Hex_Digit_Display hex_digit_display_2 (.value(divider_2_out[3:0]));  // open: dp
  LED led_2 (.in(j_k_ff_1_q));
  LED led_3 (.in(j_k_ff_2_q));
  Hex_Digit_Display hex_digit_display_3 (.value(divider_2_rem[3:0]));  // open: dp

  // Notes on the sheet:
  //   100
  //   0215
  //   10
  //   1
  //   0320
  //   042a
endmodule
